# Fritzing sketch MainProjector_v5 (saved by Fritzing 1.0.2b)

parts:
  S1 = Taiway 100-SP-X-T1 SPDT Miniature Toggle Switch [part_number=100-SP-X-T1-0-0-B1-M2 package=THT]
  Master-KRUTJAK = Arduino Pro Mini v13
  Slave-KRUTJAK = Arduino Pro Mini v13
  Драйвер_мотора = IFR520 MOS module [package=THT]
  S2 = Square Pushbutton
  btrSlave = Battery3AAA [part_number=001 package=Pack-tve]
  btrMaster = Battery3AAA [part_number=001 package=Pack-tve]
  ИКД = fc-51 [package=THT]
  M1 = gear-motor
  SG3 = Buzzer 12mm [package=buzzer-ccv]
  LED1 = LEDs [package=led10mm]
  OLED_I2C1 = OLED 128x64 I2C Monochrome Display

nets:
  GND: S1.COM, Master-KRUTJAK.GND, Slave-KRUTJAK.GND, Драйвер_мотора.GND, btrSlave.-, btrMaster.-, ИКД.pin2, M1.pin_1, SG3.2, LED1.C, OLED_I2C1.GND
  N1: S1.L1, Драйвер_мотора.VCC, S2.leg1, btrSlave.+, LED1.A
  VCC: S1.L2, Master-KRUTJAK.VCC, Slave-KRUTJAK.VCC, btrMaster.+, ИКД.pin3, OLED_I2C1.VDD
  N2: Master-KRUTJAK.A4, OLED_I2C1.SDA
  N3: Master-KRUTJAK.A5, OLED_I2C1.SCK
  N4: Master-KRUTJAK.D6_PWM, Slave-KRUTJAK.D4
  N5: Master-KRUTJAK.D5_PWM, Slave-KRUTJAK.D3_PWM
  N6: Master-KRUTJAK.D3_PWM, SG3.1
  N7: Master-KRUTJAK.D2, ИКД.pin1
  N8: Slave-KRUTJAK.D7, Драйвер_мотора.SIG
  N9: Slave-KRUTJAK.D6_PWM, Драйвер_мотора.V-
  N10: Драйвер_мотора.VIN, S2.leg0, M1.pin_2

custom parts:
  Battery3AAA: Блок 3 элементов питания AAA по 1.5В
