# Fritzing sketch MainSwitch1g2v (saved by Fritzing 1.0.2b)

parts:
  btrMaster = Battery3AA-A [part_number=001 package=Pack-tve]
  btrSlave = Battery3AA-A [part_number=001 package=Pack-tve]
  S1 = Taiway 100-SP-X-T1 SPDT Miniature Toggle Switch [part_number=100-SP-X-T1-0-0-B1-M2 package=THT]
  Master-KRUTJAK = Arduino Pro Mini v13
  Slave-KRUTJAK = Arduino Pro Mini v13
  M1 = gear-motor
  Компонент1 = IFR520 MOS module [package=THT]  # not connected
  S2 = Square Pushbutton

nets:
  GND: btrMaster.-, btrSlave.-, S1.COM, Master-KRUTJAK.GND, Slave-KRUTJAK.GND
  N1: btrSlave.+, M1.pin_1
  N2: S1.L1, S2.leg1
  N3: M1.pin_2, S2.leg0

custom parts:
  Battery3AA-A: Блок 3 элементов питания AAA по 1.5В
